// Logisim project cpu.circ as structural Verilog: 11 circuits, main circuit main
module main (
  input  Reset
);

  wire ALUinB, and_1_out, and_2_out, beqz, blt, ClockFall, ClockRise, DMwe, inp1, j, jal, jr, jump,
       keyboard_1_avail, memory_latch_1_oe_latched, memory_latch_1_we_latched, Neg, or_1_out, out1, Rdst,
       rwd, Rwe, Zero;
  wire [2:0] ALUop, multiplexer_2_out, multiplexer_4_out, Rd, Rs, Rt, shamt;
  wire [3:0] opcode;
  wire [5:0] immediate;
  wire [6:0] bit_extender_1_out;
  wire [7:0] inp2;
  wire [11:0] address;
  wire [15:0] alu_1_outputdata, cProgCount, immsign, memory_latch_1_address_latched,
       memory_latch_1_data_in_latched, multiplexer_1_out, multiplexer_3_out, multiplexer_5_out,
       multiplexer_6_out, multiplexer_7_out, multiplexer_8_out, multiplexer_9_out, ram_1_dout, reg1res,
       reg2res, rom_1_data, singleregister_1_dataout, sixteenbitadder_2_result;

  Clock clock_1 (.out(ClockRise));
  not not_1 (ClockFall, ClockRise);
  singleRegister singleregister_1 (
    .clk(ClockFall), .writeEnable(1'b1), .DataIn(multiplexer_5_out), .reset(Reset),
    .DataOut(singleregister_1_dataout));
  ROM #(.addrWidth(16), .dataWidth(16)) rom_1 (.addr(singleregister_1_dataout), .data(rom_1_data));
  SixteenBitAdder sixteenbitadder_1 (
    .sub(1'b0), .A(singleregister_1_dataout), .B(16'h1), .result(cProgCount));  // open: ovf
  instrDecoder instrdecoder_1 (
    .opcode(opcode), .input1(inp1), .output1(out1), .j(j), .jr(jr), .jal(jal), .rwd(rwd), .DMwe(DMwe),
    .ALUinB(ALUinB), .Rwe(Rwe), .Rdst(Rdst), .ALUop(ALUop), .beqz(beqz), .blt(blt), .jump(jump));
  SixteenBitAdder sixteenbitadder_2 (
    .sub(1'b0), .A(cProgCount), .B(immsign), .result(sixteenbitadder_2_result));  // open: ovf
  opDecoder opdecoder_1 (
    .Instr(rom_1_data), .address(address), .immediate(immediate), .shamt(shamt), .Rd(Rd), .Rt(Rt), .Rs(Rs),
    .opcode(opcode));
  Multiplexer #(.width(16), .enable("false")) multiplexer_1 (
    .in0(cProgCount), .in1(sixteenbitadder_2_result), .out(multiplexer_1_out), .sel(or_1_out));
  or or_1 (or_1_out, and_1_out, and_2_out);
  and and_1 (and_1_out, Zero, beqz);
  and and_2 (and_2_out, Neg, blt);
  Multiplexer #(.width(3), .enable("false")) multiplexer_2 (.in0(Rt), .in1(Rd), .out(multiplexer_2_out), .sel(Rdst));
  Multiplexer #(.width(16), .enable("false")) multiplexer_3 (
    .in0(multiplexer_1_out), .in1({4'b0000, address}), .out(multiplexer_3_out), .sel(jump));
  Multiplexer #(.width(3), .enable("false")) multiplexer_4 (
    .in0(multiplexer_2_out), .in1(3'b111), .out(multiplexer_4_out), .sel(jump));
  Multiplexer #(.width(16), .enable("false")) multiplexer_5 (
    .in0(multiplexer_3_out), .in1(reg1res), .out(multiplexer_5_out), .sel(jr));
  Bit_Extender #(.in_width(16), .out_width(7)) bit_extender_1 (.in(reg1res), .out(bit_extender_1_out));
  RegisterFile registerfile_1 (
    .writeData(multiplexer_7_out), .clk(ClockRise), .RegWriteEnable(Rwe), .reset(Reset),
    .writeReg(multiplexer_4_out), .ReadReg1(Rs), .ReadReg2(Rt), .reg1res(reg1res), .reg2res(reg2res));
  assign immsign = {{10{immediate[5]}}, immediate};  // Bit_Extender bit_extender_2
  TTY #(.rows(13), .cols(80)) tty_1 (.data(bit_extender_1_out), .clk(ClockRise), .we(out1), .clr(Reset));
  Keyboard keyboard_1 (.clk(ClockFall), .re(inp1), .clr(Reset), .avail(keyboard_1_avail), .data(inp2[6:0]));
  Multiplexer #(.width(16), .enable("false")) multiplexer_6 (
    .in0(reg2res), .in1(immsign), .out(multiplexer_6_out), .sel(ALUinB));
  not not_2 (inp2[7], keyboard_1_avail);
  ALU alu_1 (
    .Input1(reg1res), .Input2(multiplexer_6_out), .Opcode(ALUop), .Shiftnum(shamt), .zero(Zero),
    .outputData(alu_1_outputdata), .neg(Neg));
  RAM #(.addrWidth(16), .dataWidth(16), .trigger("high"), .databus("bibus")) ram_1 (
    .addr(memory_latch_1_address_latched), .we(memory_latch_1_we_latched), .oe(memory_latch_1_oe_latched),
    .din(memory_latch_1_data_in_latched), .dout(ram_1_dout));
  memory_latch memory_latch_1 (
    .address(alu_1_outputdata), .WE(DMwe), .clk(ClockFall), .data_in(reg2res),
    .address_latched(memory_latch_1_address_latched), .WE_latched(memory_latch_1_we_latched),
    .OE_latched(memory_latch_1_oe_latched), .data_in_latched(memory_latch_1_data_in_latched));
  Multiplexer #(.width(16), .enable("false")) multiplexer_7 (
    .in0(multiplexer_8_out), .in1(cProgCount), .out(multiplexer_7_out), .sel(jump));
  Multiplexer #(.width(16), .enable("false")) multiplexer_8 (
    .in0(multiplexer_9_out), .in1({{8{1'b0}}, inp2}), .out(multiplexer_8_out), .sel(inp1));
  Multiplexer #(.width(16), .enable("false")) multiplexer_9 (
    .in0(alu_1_outputdata), .in1(ram_1_dout), .out(multiplexer_9_out), .sel(rwd));

  // Notes on the sheet:
  //   Should the muxes be flipped?
endmodule

module onebitadder (
  input  Cin,
  input  A,
  input  B,
  output Sum,
  output Cout
);

  wire and_1_out, and_2_out, xor_1_out;

  xor xor_1 (xor_1_out, A, B);
  and and_1 (and_1_out, A, B);
  xor xor_2 (Sum, xor_1_out, Cin);
  and and_2 (and_2_out, xor_1_out, Cin);
  or or_1 (Cout, and_2_out, and_1_out);
endmodule

module SixteenBitAdder (
  input  sub,
  input  [15:0] A,
  input  [15:0] B,
  output [15:0] result,
  output ovf
);

  wire onebitadder_1_cout, onebitadder_2_cout, onebitadder_3_cout, onebitadder_4_cout, onebitadder_5_cout,
       onebitadder_6_cout, onebitadder_7_cout, onebitadder_8_cout, onebitadder_9_cout, onebitadder_10_cout,
       onebitadder_11_cout, onebitadder_12_cout, onebitadder_13_cout, onebitadder_14_cout,
       onebitadder_15_cout, onebitadder_16_cout, xor_1_out, xor_2_out, xor_3_out, xor_4_out, xor_5_out,
       xor_6_out, xor_7_out, xor_8_out, xor_9_out, xor_10_out, xor_11_out, xor_12_out, xor_13_out,
       xor_14_out, xor_15_out, xor_16_out;

  xor xor_1 (xor_1_out, B[0], sub);
  xor xor_2 (xor_2_out, B[1], sub);
  xor xor_3 (xor_3_out, B[2], sub);
  xor xor_4 (xor_4_out, B[3], sub);
  xor xor_5 (xor_5_out, B[4], sub);
  xor xor_6 (xor_6_out, B[5], sub);
  xor xor_7 (xor_7_out, B[6], sub);
  xor xor_8 (xor_8_out, B[7], sub);
  xor xor_9 (xor_9_out, B[8], sub);
  xor xor_10 (xor_10_out, B[9], sub);
  xor xor_11 (xor_11_out, B[10], sub);
  xor xor_12 (xor_12_out, B[11], sub);
  xor xor_13 (xor_13_out, B[12], sub);
  xor xor_14 (xor_14_out, B[13], sub);
  xor xor_15 (xor_15_out, B[14], sub);
  xor xor_16 (xor_16_out, B[15], sub);
  onebitadder onebitadder_1 (.Cin(sub), .A(A[0]), .B(xor_1_out), .Sum(result[0]), .Cout(onebitadder_1_cout));
  onebitadder onebitadder_2 (
    .Cin(onebitadder_1_cout), .A(A[1]), .B(xor_2_out), .Sum(result[1]), .Cout(onebitadder_2_cout));
  onebitadder onebitadder_3 (
    .Cin(onebitadder_2_cout), .A(A[2]), .B(xor_3_out), .Sum(result[2]), .Cout(onebitadder_3_cout));
  onebitadder onebitadder_4 (
    .Cin(onebitadder_3_cout), .A(A[3]), .B(xor_4_out), .Sum(result[3]), .Cout(onebitadder_4_cout));
  onebitadder onebitadder_5 (
    .Cin(onebitadder_4_cout), .A(A[4]), .B(xor_5_out), .Sum(result[4]), .Cout(onebitadder_5_cout));
  onebitadder onebitadder_6 (
    .Cin(onebitadder_5_cout), .A(A[5]), .B(xor_6_out), .Sum(result[5]), .Cout(onebitadder_6_cout));
  onebitadder onebitadder_7 (
    .Cin(onebitadder_6_cout), .A(A[6]), .B(xor_7_out), .Sum(result[6]), .Cout(onebitadder_7_cout));
  onebitadder onebitadder_8 (
    .Cin(onebitadder_7_cout), .A(A[7]), .B(xor_8_out), .Sum(result[7]), .Cout(onebitadder_8_cout));
  onebitadder onebitadder_9 (
    .Cin(onebitadder_8_cout), .A(A[8]), .B(xor_9_out), .Sum(result[8]), .Cout(onebitadder_9_cout));
  onebitadder onebitadder_10 (
    .Cin(onebitadder_9_cout), .A(A[9]), .B(xor_10_out), .Sum(result[9]), .Cout(onebitadder_10_cout));
  onebitadder onebitadder_11 (
    .Cin(onebitadder_10_cout), .A(A[10]), .B(xor_11_out), .Sum(result[10]), .Cout(onebitadder_11_cout));
  onebitadder onebitadder_12 (
    .Cin(onebitadder_11_cout), .A(A[11]), .B(xor_12_out), .Sum(result[11]), .Cout(onebitadder_12_cout));
  onebitadder onebitadder_13 (
    .Cin(onebitadder_12_cout), .A(A[12]), .B(xor_13_out), .Sum(result[12]), .Cout(onebitadder_13_cout));
  onebitadder onebitadder_14 (
    .Cin(onebitadder_13_cout), .A(A[13]), .B(xor_14_out), .Sum(result[13]), .Cout(onebitadder_14_cout));
  onebitadder onebitadder_15 (
    .Cin(onebitadder_14_cout), .A(A[14]), .B(xor_15_out), .Sum(result[14]), .Cout(onebitadder_15_cout));
  onebitadder onebitadder_16 (
    .Cin(onebitadder_15_cout), .A(A[15]), .B(xor_16_out), .Sum(result[15]), .Cout(onebitadder_16_cout));
  xor xor_17 (ovf, onebitadder_15_cout, onebitadder_16_cout);
endmodule

module lShift (
  input  [15:0] data_in,
  input  [2:0] shift,
  output [15:0] data_out
);

  wire [15:0] multiplexer_1_out, multiplexer_2_out;

  Multiplexer #(.width(16), .enable("false")) multiplexer_1 (
    .in0(data_in), .in1({data_in[14:0], 1'b0}), .out(multiplexer_1_out), .sel(shift[0]));
  Multiplexer #(.width(16), .enable("false")) multiplexer_2 (
    .in0(multiplexer_1_out), .in1({multiplexer_1_out[13:0], 2'b00}), .out(multiplexer_2_out), .sel(shift[1]));
  Multiplexer #(.width(16), .enable("false")) multiplexer_3 (
    .in0(multiplexer_2_out), .in1({multiplexer_2_out[11:0], 4'b0000}), .out(data_out), .sel(shift[2]));

  // Other names for the same wires on the sheet: S0 = shift[0]; S1 = shift[1]; S2 = shift[2]
endmodule

module rShift (
  input  [15:0] data_in,
  input  [2:0] shift,
  output [15:0] data_out
);

  wire [15:0] multiplexer_1_out, multiplexer_2_out;

  Multiplexer #(.width(16), .enable("false")) multiplexer_1 (
    .in0(data_in), .in1({1'b0, data_in[15:1]}), .out(multiplexer_1_out), .sel(shift[0]));
  Multiplexer #(.width(16), .enable("false")) multiplexer_2 (
    .in0(multiplexer_1_out), .in1({2'b00, multiplexer_1_out[15:2]}), .out(multiplexer_2_out), .sel(shift[1]));
  Multiplexer #(.width(16), .enable("false")) multiplexer_3 (
    .in0(multiplexer_2_out), .in1({4'b0000, multiplexer_2_out[15:4]}), .out(data_out), .sel(shift[2]));

  // Other names for the same wires on the sheet: S0 = shift[0]; S1 = shift[1]; S2 = shift[2]
endmodule

module ALU (
  input  [15:0] Input1,
  input  [15:0] Input2,
  input  [2:0] Opcode,
  input  [2:0] Shiftnum,
  output zero,
  output [15:0] outputData,
  output neg
);

  wire or_1_out;
  wire [15:0] lshift_1_data_out, not_2_out, rshift_1_data_out, sixteenbitadder_1_result,
       sixteenbitadder_2_result, xor_1_out;

  or or_1 (or_1_out, Input1[0], Input1[1], Input1[2], Input1[3], Input1[4], Input1[5], Input1[6], Input1[7], Input1[9], Input1[10], Input1[11], Input1[12], Input1[13], Input1[14], Input1[15], Input1[8]);
  not not_1 (zero, or_1_out);
  SixteenBitAdder sixteenbitadder_1 (
    .sub(1'b0), .A(Input1), .B(Input2), .result(sixteenbitadder_1_result));  // open: ovf
  SixteenBitAdder sixteenbitadder_2 (
    .sub(1'b1), .A(Input1), .B(Input2), .result(sixteenbitadder_2_result));  // open: ovf
  lShift lshift_1 (.data_in(Input1), .shift(Shiftnum), .data_out(lshift_1_data_out));
  rShift rshift_1 (.data_in(Input1), .shift(Shiftnum), .data_out(rshift_1_data_out));
  assign xor_1_out = Input1 ^ Input2;  // XOR_Gate xor_1, 16 bits wide
  assign not_2_out = ~Input1;  // NOT_Gate not_2, 16 bits wide
  Multiplexer #(.select(3), .width(16), .enable("false")) multiplexer_1 (
    .in0(sixteenbitadder_1_result), .in1(sixteenbitadder_2_result), .in2(not_2_out), .in3(xor_1_out),
    .in4(lshift_1_data_out), .in5(rshift_1_data_out), .out({neg, outputData[14:0]}), .sel(Opcode));  // open: in6, in7

  assign outputData[15] = neg;

  // Other names for the same wires on the sheet: I1[15:0] = Input1; I2[15:0] = Input2; Snum[2:0] = Shiftnum
endmodule

module singleRegister (
  input  clk,
  input  writeEnable,
  input  [15:0] DataIn,
  input  reset,
  output [15:0] DataOut
);

  wire clk_t;

  and and_1 (clk_t, clk, writeEnable);
  D_Flip_Flop d_ff_1 (.D(DataIn[0]), .clk(clk_t), .Q(DataOut[0]), .reset(reset));  // open: Qn, preset
  D_Flip_Flop d_ff_2 (.D(DataIn[3]), .clk(clk_t), .Q(DataOut[3]), .reset(reset));  // open: Qn, preset
  D_Flip_Flop d_ff_3 (.D(DataIn[6]), .clk(clk_t), .Q(DataOut[6]), .reset(reset));  // open: Qn, preset
  D_Flip_Flop d_ff_4 (.D(DataIn[9]), .clk(clk_t), .Q(DataOut[9]), .reset(reset));  // open: Qn, preset
  D_Flip_Flop d_ff_5 (.D(DataIn[12]), .clk(clk_t), .Q(DataOut[12]), .reset(reset));  // open: Qn, preset
  D_Flip_Flop d_ff_6 (.D(DataIn[1]), .clk(clk_t), .Q(DataOut[1]), .reset(reset));  // open: Qn, preset
  D_Flip_Flop d_ff_7 (.D(DataIn[4]), .clk(clk_t), .Q(DataOut[4]), .reset(reset));  // open: Qn, preset
  D_Flip_Flop d_ff_8 (.D(DataIn[7]), .clk(clk_t), .Q(DataOut[7]), .reset(reset));  // open: Qn, preset
  D_Flip_Flop d_ff_9 (.D(DataIn[10]), .clk(clk_t), .Q(DataOut[10]), .reset(reset));  // open: Qn, preset
  D_Flip_Flop d_ff_10 (.D(DataIn[13]), .clk(clk_t), .Q(DataOut[13]), .reset(reset));  // open: Qn, preset
  D_Flip_Flop d_ff_11 (.D(DataIn[2]), .clk(clk_t), .Q(DataOut[2]), .reset(reset));  // open: Qn, preset
  D_Flip_Flop d_ff_12 (.D(DataIn[5]), .clk(clk_t), .Q(DataOut[5]), .reset(reset));  // open: Qn, preset
  D_Flip_Flop d_ff_13 (.D(DataIn[8]), .clk(clk_t), .Q(DataOut[8]), .reset(reset));  // open: Qn, preset
  D_Flip_Flop d_ff_14 (.D(DataIn[11]), .clk(clk_t), .Q(DataOut[11]), .reset(reset));  // open: Qn, preset
  D_Flip_Flop d_ff_15 (.D(DataIn[14]), .clk(clk_t), .Q(DataOut[14]), .reset(reset));  // open: Qn, preset
  D_Flip_Flop d_ff_16 (.D(DataIn[15]), .clk(clk_t), .Q(DataOut[15]), .reset(reset));  // open: Qn, preset

  // Other names for the same wires on the sheet: D0 = DataIn[0]; D1 = DataIn[1]; D2 = DataIn[2]; D3 = DataIn[3];
  //   D4 = DataIn[4]; D5 = DataIn[5]; D6 = DataIn[6]; D7 = DataIn[7]; D8 = DataIn[8]; D9 = DataIn[9];
  //   D10 = DataIn[10]; D11 = DataIn[11]; D12 = DataIn[12]; D13 = DataIn[13]; D14 = DataIn[14]; D15 = DataIn[15];
  //   Q0 = DataOut[0]; Q1 = DataOut[1]; Q2 = DataOut[2]; Q3 = DataOut[3]; Q4 = DataOut[4]; Q5 = DataOut[5];
  //   Q6 = DataOut[6]; Q7 = DataOut[7]; Q8 = DataOut[8]; Q9 = DataOut[9]; Q10 = DataOut[10]; Q11 = DataOut[11];
  //   Q12 = DataOut[12]; Q13 = DataOut[13]; Q14 = DataOut[14]; Q15 = DataOut[15]; R = reset
endmodule

module RegisterFile (
  input  [15:0] writeData,
  input  clk,
  input  RegWriteEnable,
  input  reset,
  input  [2:0] writeReg,
  input  [2:0] ReadReg1,
  input  [2:0] ReadReg2,
  output [15:0] reg1res,
  output [15:0] reg2res
);

  wire a0, a1, a2, a3, a4, a5, a6, a7, b0, b1, b2, b3, b4, b5, b6, b7, clk_t, undriven, undriven_2, We0, We1,
       We2, We3, We4, We5, We6, We7;
  wire [15:0] outp0, outp1, outp2, outp3, outp4, outp5, outp6, outp7;

  Decoder #(.select(3)) decoder_1 (
    .out0(We0), .out1(We1), .out2(We2), .out3(We3), .out4(We4), .out5(We5), .out6(We6), .out7(We7),
    .sel(writeReg), .en(clk_t));
  Decoder #(.select(3)) decoder_2 (
    .out0(a0), .out1(a1), .out2(a2), .out3(a3), .out4(a4), .out5(a5), .out6(a6), .out7(a7), .sel(ReadReg1),
    .en(undriven));
  Decoder #(.select(3)) decoder_3 (
    .out0(b0), .out1(b1), .out2(b2), .out3(b3), .out4(b4), .out5(b5), .out6(b6), .out7(b7), .sel(ReadReg2),
    .en(undriven_2));
  and and_1 (clk_t, clk, RegWriteEnable);
  // Probe on outp1
  singleRegister singleregister_1 (.clk(clk_t), .writeEnable(We1), .DataIn(writeData), .reset(reset), .DataOut(outp1));
  // Probe on outp2
  singleRegister singleregister_2 (.clk(clk_t), .writeEnable(We2), .DataIn(writeData), .reset(reset), .DataOut(outp2));
  // Probe on outp3
  singleRegister singleregister_3 (.clk(clk_t), .writeEnable(We3), .DataIn(writeData), .reset(reset), .DataOut(outp3));
  singleRegister singleregister_4 (.clk(clk_t), .writeEnable(We4), .DataIn(writeData), .reset(reset), .DataOut(outp4));
  singleRegister singleregister_5 (.clk(clk_t), .writeEnable(We5), .DataIn(writeData), .reset(reset), .DataOut(outp5));
  singleRegister singleregister_6 (.clk(clk_t), .writeEnable(We6), .DataIn(writeData), .reset(reset), .DataOut(outp6));
  singleRegister singleregister_7 (.clk(clk_t), .writeEnable(We7), .DataIn(writeData), .reset(reset), .DataOut(outp7));
  singleRegister singleregister_8 (.clk(clk_t), .writeEnable(We0), .DataIn({16{1'b0}}), .reset(reset), .DataOut(outp0));
  // Probe on outp4
  // Probe on outp5
  // Probe on outp6
  // Probe on outp7
  // Probe on outp0
  assign reg1res = a1 ? outp1 : 16'bz;  // Controlled_Buffer controlled_buffer_1
  assign reg1res = a2 ? outp2 : 16'bz;  // Controlled_Buffer controlled_buffer_2
  assign reg1res = a3 ? outp3 : 16'bz;  // Controlled_Buffer controlled_buffer_3
  assign reg1res = a4 ? outp4 : 16'bz;  // Controlled_Buffer controlled_buffer_4
  assign reg1res = a5 ? outp5 : 16'bz;  // Controlled_Buffer controlled_buffer_5
  assign reg1res = a6 ? outp6 : 16'bz;  // Controlled_Buffer controlled_buffer_6
  assign reg1res = a7 ? outp7 : 16'bz;  // Controlled_Buffer controlled_buffer_7
  assign reg1res = a0 ? outp0 : 16'bz;  // Controlled_Buffer controlled_buffer_8
  assign reg2res = b1 ? outp1 : 16'bz;  // Controlled_Buffer controlled_buffer_9
  assign reg2res = b2 ? outp2 : 16'bz;  // Controlled_Buffer controlled_buffer_10
  assign reg2res = b3 ? outp3 : 16'bz;  // Controlled_Buffer controlled_buffer_11
  assign reg2res = b4 ? outp4 : 16'bz;  // Controlled_Buffer controlled_buffer_12
  assign reg2res = b5 ? outp5 : 16'bz;  // Controlled_Buffer controlled_buffer_13
  assign reg2res = b6 ? outp6 : 16'bz;  // Controlled_Buffer controlled_buffer_14
  assign reg2res = b7 ? outp7 : 16'bz;  // Controlled_Buffer controlled_buffer_15
  assign reg2res = b0 ? outp0 : 16'bz;  // Controlled_Buffer controlled_buffer_16

  // Other names for the same wires on the sheet: R = reset
endmodule

module memory_latch (
  input  [15:0] address,
  input  WE,
  input  clk,
  input  [15:0] data_in,
  output [15:0] address_latched,
  output WE_latched,
  output OE_latched,
  output [15:0] data_in_latched
);

  wire DMwe_latch_q;
  wire [15:0] addr_latch_q;

  Register #(.width(16), .trigger("falling")) addr_latch (
    .D(address), .en(WE), .clk(clk), .Q(addr_latch_q));  // open: clr
  D_Flip_Flop #(.trigger("falling")) DMwe_latch (.D(WE), .clk(clk), .Q(DMwe_latch_q));  // open: Qn, preset, reset
  Register #(.width(16), .trigger("falling")) data_to_be_written (
    .D(data_in), .en(WE), .clk(clk), .Q(data_in_latched));  // open: clr
  Multiplexer #(.width(16), .enable("false")) multiplexer_1 (
    .in0(address), .in1(addr_latch_q), .out(address_latched), .sel(DMwe_latch_q));
  and and_1 (WE_latched, clk, DMwe_latch_q);
  not not_1 (OE_latched, WE_latched);
endmodule

module instrDecoder (
  input  [3:0] opcode,
  output input1,
  output output1,
  output j,
  output jr,
  output jal,
  output rwd,
  output DMwe,
  output ALUinB,
  output Rwe,
  output Rdst,
  output [2:0] ALUop,
  output beqz,
  output blt,
  output jump
);

  wire decoder_1_out0, decoder_1_out1, decoder_1_out2, decoder_1_out3, decoder_1_out4, decoder_1_out5,
       decoder_1_out6;

  Decoder #(.select(4)) decoder_1 (
    .out0(decoder_1_out0), .out1(decoder_1_out1), .out2(decoder_1_out2), .out3(decoder_1_out3),
    .out4(decoder_1_out4), .out5(decoder_1_out5), .out6(decoder_1_out6), .out7(rwd), .out8(DMwe),
    .out9(beqz), .out10(blt), .out11(j), .out12(jr), .out13(jal), .out14(input1), .out15(output1),
    .sel(opcode));  // open: en
  or or_1 (ALUinB, decoder_1_out2, rwd, DMwe);
  or or_2 (Rdst, decoder_1_out0, decoder_1_out1, decoder_1_out3, decoder_1_out4, decoder_1_out5, decoder_1_out6, input1);
  or or_3 (ALUop[2], decoder_1_out5, decoder_1_out6);
  or or_4 (jump, j, jal);
  or or_5 (ALUop[1], decoder_1_out3, decoder_1_out4);
  or or_6 (ALUop[0], decoder_1_out1, decoder_1_out4, decoder_1_out6, blt);
  or or_7 (Rwe, decoder_1_out0, decoder_1_out1, decoder_1_out2, decoder_1_out3, decoder_1_out4, decoder_1_out5, decoder_1_out6, rwd, input1, jal);

  // Notes on the sheet:
  //   j
  //   jr
  //   Add
  //   Sub
  //   Addi
  //   Not
  //   xor
  //   sll
  //   srl
  //   lw
  //   sw
  //   beqz
  //   blt
  //   jal
  //   input
  //   output
endmodule

module opDecoder (
  input  [15:0] Instr,
  output [11:0] address,
  output [5:0] immediate,
  output [2:0] shamt,
  output [2:0] Rd,
  output [2:0] Rt,
  output [2:0] Rs,
  output [3:0] opcode
);


  assign address = Instr[11:0];
  assign immediate = Instr[5:0];
  assign opcode = Instr[15:12];
  assign Rd = Instr[5:3];
  assign Rs = Instr[11:9];
  assign Rt = Instr[8:6];
  assign shamt = Instr[2:0];
endmodule
